# Fritzing sketch Button (saved by Fritzing 0.9.3b)
breadboards: 1

parts:
  Raspberry_Pi_1 = Raspberry Pi 3 [part_number=RPI-3-V1.2]
  LED1 = LED - 5mm [color="Red (633nm)" package="5 mm [THT]"]
  S1 = Pushbutton [package="[SMD]"]

nets:
  N1: Raspberry_Pi_1.GND, S1.Pin_3, S1.Pin_4
  N2: Raspberry_Pi_1.GPIO24, LED1.anode
  N3: S1.Pin_1, S1.Pin_2
