# Fritzing sketch Sonar (saved by Fritzing 0.9.3b)
breadboards: 1

parts:
  Raspberry_Pi_1 = Raspberry Pi 3 [part_number=RPI-3-V1.2]
  hc-sr1 = hc-sr04
  R1 = Resistor [tolerance=±5% resistance=47k package="1206 [SMD]"]
  R2 = Resistor [tolerance=±5% resistance=10k package="1206 [SMD]"]

nets:
  N1: Raspberry_Pi_1.GPIO19, hc-sr1.Trig
  N2: Raspberry_Pi_1.GPIO26, R1.Pin_1, R2.Pin_0
  GND: Raspberry_Pi_1.GND, hc-sr1.GND
  5V: Raspberry_Pi_1.5V, hc-sr1.VCC, R2.Pin_1
  N3: hc-sr1.Echo, R1.Pin_0
